# Fritzing sketch Circuit diagram (saved by Fritzing 0.8.7b)
breadboards: 1

parts:
  Part1 = Arduino Uno (Rev3)
  Part5 = SRF05 Ultrasonic Rangefinder
  R1 = Rotary Potentiometer (Small) [maximum_resistance=100kΩ package=THT]
  LCD1 = LCD screen
  Part7 = SRF05 Ultrasonic Rangefinder
  Part8 = SRF05 Ultrasonic Rangefinder
  R2 = Resistor [tolerance=±5% resistance=220 package=THT]

nets:
  N1: Part1.D8, Part7.Echo
  N2: Part1.D9_PWM, Part7.Trig
  N3: Part1.D10_PWM/SS, Part5.Trig
  N4: Part1.D11_PWM/MOSI, Part8.Trig
  N5: Part1.D12/MISO, Part8.Echo
  N6: Part1.D13/SCK, Part5.Echo
  N7: Part1.D1/TX, LCD1.RS
  N8: Part1.D2, LCD1.E
  N9: Part1.D4, LCD1.DB4
  N10: Part1.D5_PWM, LCD1.DB5
  N11: Part1.D6_PWM, LCD1.DB6
  N12: Part1.D7, LCD1.DB7
  5V: Part1.5V, R1.leg2, LCD1.VDD, R2.Pin_0
  N13: Part1.GND, R1.leg1, LCD1.LED-
  N14: R1.wiper, LCD1.V0
  N15: LCD1.LED+, R2.Pin_1
